# Fritzing sketch QtPy-ESP32S2 2 (saved by Fritzing 0.9.10b)
breadboards: 1

parts:
  Part2 = Adafruit TPL5110 Power Timer [part_number="Adafruit #3435"]
  Part3 = Adafruit BQ24074 Solar-DC-USB Lipo Charger
  U1 = LIPO-2000mAh [package=lipo-2000]
  Part4 = Adafruit LiPoly Charger BFF for QT Py [part_number="Adafruit #5397"]
  Part6 = Soil Moisture Sensor
  R2 = Resistor [tolerance=±1% power=0.25 resistance=12k package=THT]
  J1 = Camdenboss CTB0158-2 [part_number=CTB0158-2 package=THT]
  Adafruit_microSD_Card_BFF1 = Adafruit microSD Card BFF [part_number=#5683]
  ZS-042_RTC1 = ZS-042 RTC Module
  LED1 = LED - 5mm [color="Red (633nm)" current=0.030 package="5 mm [THT]"]
  LED2 = LED - 5mm [color="Green (565nm)" current=0.030 package="5 mm [THT]"]
  R3 = Resistor [tolerance=±5% power=0.25 resistance=330 package=THT]
  R4 = Resistor [tolerance=±5% power=0.25 resistance=330 package=THT]
  Part7 = Adafruit AHT20 Temperature and Humidity Sensor [part_number="Adafruit #4566"]
  Part10 = Adafruit BME280 [part_number="Adafruit #2652"]
  Part11 = Adafruit BME680 [part_number="Adafruit #3660"]
  R5 = Resistor [tolerance=±1% power=0.25 resistance=3k package=THT]
  Part5 = Adafruit QT Py ESP32-S2 [part_number="Adafruit #5325"]
  Part12 = Adafruit SHT4x [part_number="Adafruit #4885"]

nets:
  N1: Part2.VDD, Part3.OUT
  GND: Part2.GND, Part3.GND, Part3.D+, U1.-, Part4.GND, Part6.GND, J1.pin1, Adafruit_microSD_Card_BFF1.GND, ZS-042_RTC1.GND, LED1.cathode, LED2.cathode, Part7.GND, Part10.GND, Part11.GND, R5.Pin_0, Part5.GND, Part12.GND
  N2: Part2.PWROUT, Part4.VBAT, R4.Pin_1
  N3: Part2.DONE, R3.Pin_1, Part5.RX
  N4: Part3.VLIPO, U1.+
  N5: Part3.D-, Part3.THERM
  N6: Part4.A2, Part5.A2
  +5V: Part4.+5V, Part5.+5V
  N7: Part6.SIG, Part5.A3
  VCC: Part6.VCC, ZS-042_RTC1.VCC, Part7.VCC, Part10.VCC, Part11.VCC, Part5.3.3V, Part12.VCC
  N8: R2.Pin_0, J1.pin2
  N9: R2.Pin_1, R5.Pin_1, Part5.A1
  N10: Adafruit_microSD_Card_BFF1.TX, Part5.TX
  N11: Adafruit_microSD_Card_BFF1.SCK, Part5.SCK
  N12: Adafruit_microSD_Card_BFF1.MISO, Part5.MISO
  N13: Adafruit_microSD_Card_BFF1.MOSI, Part5.MOSI
  N14: ZS-042_RTC1.SDA, Part7.SDA, Part10.SDI/SDA, Part11.SDI/SDA, Part5.SDA1, Part12.SDA
  N15: ZS-042_RTC1.SCL, Part7.SCL, Part10.SCK/SCL, Part11.SCK/SCL, Part5.SCL1, Part12.SCL
  N16: LED1.anode, R3.Pin_0
  N17: LED2.anode, R4.Pin_0

notes:
  All sensors are chained with Stemma QT cables, except the soil moisture sensor.
  The breadboard rails are GND and the 3.3v from the QtPy.
  This connector is wired to the 12v battery terminals. A voltage divider is used to insure we don't fry the QtPy.
  The TPL5110 switches VDD on & off to the QtPy LiPo BFF.
  It connects VDD to the DRV pin every 5 min and when the QtPy signals DONE using its RX pin, the TPL5110 disconnects VDD from the DRV pin.
  The QtPy LiPo BFF supplies power to the QtPy's 5V pin, and outputs a voltage reading of the incoming power, via the A2 pin.
  The solar/USB charger charges the battery and supplies power to the VDD pin of the TPL5110 power switcher.
  GREEN - QtPy power on
  RED - QtPy's DONE signal
  The QtPy logs everything to a 16GB microSD card. The QtPy SDcard BFF is connected using SPI and selected with the QtPy's TX pin.
  A0 - NC
  A1 - !/5th of 12V battery (3/15)
  A2 - BFF battery measurement
  A3 - Soil probe voltage
  A DS3231 Real-time-clock (RTC) is used to timestamp log records. An onboard Flash memory is used to store a flag indicating we've set the time of the RTC to a NTP source.

custom parts:
  Adafruit TPL5110 Power Timer: With some development boards, low power usage is an afterthought. Especially when price and usability is the main selling point. So what should you do when its time to turn around and make that project of yours run on a battery or solar? Sure you could try to hot-air that regulator off, or you could jerry-rig a relay. Or, use a 555? Ugh, the options aren't that great. The Adafruit TPL5110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
  Adafruit LiPoly Charger BFF for QT Py: Is your QT Py all alone, lacking a friend to travel the wide world with? When you were a kid you may have learned about the "buddy" system, well this product is kinda like that! A board that will watch your QT Py's back and give it the power and support to wander out past your USB port. This little lipo charger is designed to fit onto the back of any QT Py board, and make it easy for portable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
  Adafruit microSD Card BFF: Our QT Py boards are a great way to make very small microcontroller projects that pack a ton of power - and now we have a way for you to add a ton of storage, for reading and writing, with a micro SD card slot that can fit on the back of your miniature dev board. It uses the three SPI pins plus one chip select pin to access megs or gigs of data. We call this the Adafruit microSD BFF - a "Best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
  Adafruit AHT20 Temperature and Humidity Sensor: The AHT20 is a nice but inexpensive temperature and humidity sensor from the same folks that brought us the DHT22. You can take sensor readings as often as you like, and it uses standard I2C so its super easy to use with any Arduino or Linux/Raspberry Pi board. This sensor has a typical accuracy of +- 2% relative humidity, and +-0.3 °C. There is only one I2C address so its not a good option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
  Adafruit BME280: Bosch has stepped up their game with their new BME280 sensor, an environmental sensor with temperature, barometric pressure and humidity! This sensor is great for all sorts of indoor environmental sensing and can even be used in both I2C and SPI! This precision sensor from Bosch is the best low-cost sensing solution for measuring humidity with ±3% accuracy, barometric pressure with ±1 hPa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
  Adafruit QT Py ESP32-S2: What has your favorite Espressif WiFi microcontroller, comes with our favorite connector - the STEMMA QT, a chainable I2C port, and has lots of Flash and RAM memory for your next IoT project? What will make your next IoT project flyyyyy? What a cutie pie! Or is it... a QT Py? This diminutive dev board comes with one of our new favorite lil chips, the ESP32-S2! The ESP32-S2 is a highly-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
  Adafruit SHT4x: Sensirion Temperature/Humidity sensors are some of the finest & highest-accuracy devices you can get. And finally, we have some that have a true I2C interface for easy reading. The SHT40 and SHT45 sensors are the fourth generation (started at the SHT10 and worked its way up to the top!). The SHT40 has an excellent ±1.8% typical relative humidity accuracy from 25 to 75% and ±0.2 °C typical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
